// Logisim project cpu1.circ as structural Verilog: 3 circuits, main circuit main
module main (
  input  [7:0] in_1,
  input  in_2,
  input  [31:0] order
);

  wire clock_1_out, not_1_out;
  wire [7:0] alu_1_o, bit_extender_1_out, multiplexer_1_out, ram_1_dout, registergroup_1_dout;

  Bit_Extender #(.in_width(10), .out_width(8)) bit_extender_1 (.in(order[15:6]), .out(bit_extender_1_out));
  Clock clock_1 (.out(clock_1_out));
  RegisterGroup registergroup_1 (
    .Din(multiplexer_1_out), .WriteAddr(order[20:16]), .ReadAddr(order[25:21]), .WriteEn(order[31]),
    .CLK(clock_1_out), .rst(in_2), .Dout(registergroup_1_dout));
  Multiplexer #(.width(8)) multiplexer_1 (.in0(alu_1_o), .in1(ram_1_dout), .out(multiplexer_1_out), .sel(order[30]));
  ALU alu_1 (.Control(order[5:0]), .A(registergroup_1_dout), .B(bit_extender_1_out), .O(alu_1_o));
  not not_1 (not_1_out, order[29]);
  RAM ram_1 (
    .addr(in_1), .we(order[29]), .oe(not_1_out), .clk(clock_1_out), .din(registergroup_1_dout),
    .dout(ram_1_dout));
endmodule

module RegisterGroup (
  input  [7:0] Din,
  input  [4:0] WriteAddr,
  input  [4:0] ReadAddr,
  input  WriteEn,
  input  CLK,
  input  rst,
  output [7:0] Dout
);

  wire decoder_1_out0, decoder_1_out1, decoder_1_out2, decoder_1_out3, decoder_1_out4, decoder_1_out5,
       decoder_1_out6, decoder_1_out7;
  wire [7:0] register_1_q, register_2_q, register_3_q, register_4_q, register_5_q, register_6_q,
       register_7_q, register_8_q;

  Decoder #(.select(3)) decoder_1 (
    .out0(decoder_1_out0), .out1(decoder_1_out1), .out2(decoder_1_out2), .out3(decoder_1_out3),
    .out4(decoder_1_out4), .out5(decoder_1_out5), .out6(decoder_1_out6), .out7(decoder_1_out7),
    .sel(WriteAddr[2:0]), .en(WriteEn));
  Register register_1 (.D(Din), .en(decoder_1_out0), .clk(CLK), .Q(register_1_q), .clr(rst));
  Register register_2 (.D(Din), .en(decoder_1_out2), .clk(CLK), .Q(register_2_q), .clr(rst));
  Register register_3 (.D(Din), .en(decoder_1_out4), .clk(CLK), .Q(register_3_q), .clr(rst));
  Register register_4 (.D(Din), .en(decoder_1_out6), .clk(CLK), .Q(register_4_q), .clr(rst));
  Register register_5 (.D(Din), .en(decoder_1_out1), .clk(CLK), .Q(register_5_q), .clr(rst));
  Register register_6 (.D(Din), .en(decoder_1_out3), .clk(CLK), .Q(register_6_q), .clr(rst));
  Register register_7 (.D(Din), .en(decoder_1_out5), .clk(CLK), .Q(register_7_q), .clr(rst));
  Register register_8 (.D(Din), .en(decoder_1_out7), .clk(CLK), .Q(register_8_q), .clr(rst));
  Multiplexer #(.select(3), .width(8)) multiplexer_1 (
    .in0(register_1_q), .in1(register_5_q), .in2(register_2_q), .in3(register_6_q), .in4(register_3_q),
    .in5(register_7_q), .in6(register_4_q), .in7(register_8_q), .out(Dout), .sel(ReadAddr[2:0]));
endmodule

module ALU (
  input  [5:0] Control,
  input  [7:0] A,
  input  [7:0] B,
  output [7:0] O
);

  Adder adder_1 (.a(A), .b(B), .out(O), .cin(1'b0));  // open: cout
endmodule
